# Fritzing sketch circuit diagram arduino (saved by Fritzing 1.0.2b)

parts:
  V1 = DC Power [voltage=5]  # not connected
  A1 = Hanmatek HM305
  C1 = JYQD-V7-3E2 motor driver
  A4 = hub motor wheel
  C2 = JYQD-V7-3E2 motor driver
  A6 = hub motor wheel
  Composant1 = Arduino Mega ADK (Rev3)
  S1 = Round Pushbutton
  F1 = FUSE [package=fuse_5mm]

nets:
  N1: A1.Pin_3, C1.Pin_15, C2.Pin_15
  N2: A1.Pin_4, F1.2
  N3: C1.Pin_1, C1.Pin_6, A4.Pin_8, C2.Pin_1, C2.Pin_6, A6.Pin_8, Composant1.GND
  N4: C1.Pin_2, A4.Pin_6
  N5: C1.Pin_3, A4.Pin_5
  N6: C1.Pin_4, A4.Pin_7
  N7: C1.Pin_5, C1.Pin_11, A4.Pin_4, C2.Pin_5, C2.Pin_11, A6.Pin_4, Composant1.5V
  N8: C1.Pin_7, Composant1.D6_PWM
  N9: C1.Pin_10, Composant1.D5_PWM
  N10: C1.Pin_12, A4.Pin_1
  N11: C1.Pin_13, A4.Pin_2
  N12: C1.Pin_14, A4.Pin_3
  N13: C1.Pin_16, C2.Pin_16, S1.leg1
  N14: C2.Pin_2, A6.Pin_6
  N15: C2.Pin_3, A6.Pin_5
  N16: C2.Pin_4, A6.Pin_7
  N17: C2.Pin_7, Composant1.D9_PWM
  N18: C2.Pin_10, Composant1.D8_PWM
  N19: C2.Pin_12, A6.Pin_1
  N20: C2.Pin_13, A6.Pin_2
  N21: C2.Pin_14, A6.Pin_3
  N22: S1.leg0, F1.1

custom parts:
  Hanmatek HM305: DC Power Supply 30V5A HM305.
  JYQD-V7-3E2 motor driver: JYQD-V7.3E2 brushless DC motor driver board.
  Round Pushbutton: A generic pushbutton.
